# Fritzing sketch OLED_HUMID_SCHEMATIC (saved by Fritzing 1.0.5)
breadboards: 1

parts:
  Part1 = SPI OLED Monochrome 128x64 0.96 inch
  RHT1 = Humidity and Temperature Sensor RHT03
  Part2 = Arduino Uno (Rev3)

nets:
  GND: Part1.GND, RHT1.GND_2, Part2.GND
  VDD: Part1.VDD, RHT1.Vcc, Part2.5V
  N1: Part1.SCK, Part2.D11_PWM/MOSI
  N2: Part1.SDA, Part2.D13/SCK
  N3: Part1.RES, Part2.D9_PWM
  N4: Part1.DC, Part2.D8
  N5: Part1.CS, Part2.D10_PWM/SS
  N6: RHT1.Data-signal, Part2.D2

custom parts:
  SPI OLED Monochrome 128x64 0.96 inch: Unknown 128x64 0.96 inch 128x64 SPI Monochrome OLED display
